# Fritzing sketch sbridb_2020 (saved by Fritzing 0.9.3b)
breadboards: 1

parts:
  Placa_Arduino_Uno_R3 = Arduino Uno (Rev3)
  Módulo_Bluetooth_HC-05 = Bluetooth HC-05 Macho
  R2 = Resistor [tolerance=±5% resistance=2.2k package=THT]
  R3 = Resistor [tolerance=±5% resistance=1k package=THT]
  BAT1 = Battery Holders [package=battery-aa]

nets:
  N1: Placa_Arduino_Uno_R3.A0, BAT1.+
  GND: Placa_Arduino_Uno_R3.GND, Módulo_Bluetooth_HC-05.GND, R2.Pin_1
  N2: Placa_Arduino_Uno_R3.D0/RX, Módulo_Bluetooth_HC-05.TXD
  N3: Placa_Arduino_Uno_R3.D1/TX, R3.Pin_0
  5V: Placa_Arduino_Uno_R3.5V, Módulo_Bluetooth_HC-05.VCC
  N4: Módulo_Bluetooth_HC-05.RXD, R2.Pin_0, R3.Pin_1

// code stored in the sketch: abat-jour_automatique.ino

